# Fritzing sketch Aflevering 2 (saved by Fritzing 0.9.9b)
breadboards: 1

parts:
  Part1 = Arduino Uno (Rev3) - ICSP
  Part2 = Arduino Motor Shield (Rev3)
  M1 = DC Motor
  M2 = DC Motor
  U1 = 74HC595 [package="DIP16 [THT]"]
  VCC3 = Battery
  VCC4 = Battery
  LED1 = LEDs [package=led10mm]
  LED2 = LEDs [package=led10mm]
  LED3 = LEDs [package=led10mm]
  LED4 = LEDs [package=led10mm]
  LED5 = LEDs [package=led10mm]
  R2 = Resistor [tolerance=±5% resistance=110 package="0603 [SMD]"]
  R3 = Resistor [tolerance=±5% resistance=110 package="0603 [SMD]"]
  R4 = Resistor [tolerance=±5% resistance=110 package="0603 [SMD]"]
  R5 = Resistor [tolerance=±5% resistance=110 package="0603 [SMD]"]
  R6 = Resistor [tolerance=±5% resistance=110 package="0603 [SMD]"]
  HC-SR04_Sensor_1 = HC-SR04 Ultrasonic Distance Sensor
  IR_Reflectance_Sensor_Front = PHOTOTRANSISTOR REFLECTIVE OBJECT SENSOR [package=qrb1114-side]
  IR_Reflectance_Sensor_Left = PHOTOTRANSISTOR REFLECTIVE OBJECT SENSOR [package=qrb1114-side]
  IR_Reflectance_Right = PHOTOTRANSISTOR REFLECTIVE OBJECT SENSOR [package=qrb1114-side]

nets:
  N1: Part1.D3_PWM, Part2.D6_PWM, HC-SR04_Sensor_1.TRIG
  N2: Part1.D6_PWM, Part2.D3_PWM/A
  VCC: Part2.A2, Part2.5V, Part2.A3, Part2.A4, U1.MR, U1.VCC, HC-SR04_Sensor_1.VCC, IR_Reflectance_Sensor_Front.A, IR_Reflectance_Sensor_Front.C, IR_Reflectance_Sensor_Left.A, IR_Reflectance_Sensor_Left.C, IR_Reflectance_Right.A, IR_Reflectance_Right.C
  N3: Part2.GND, U1.OE, VCC3.-, VCC4.-
  N4: Part2.A5, HC-SR04_Sensor_1.ECHO
  N5: Part2.D4, U1.ST_CP
  N6: Part2.D5_PWM, U1.SH_CP
  N7: Part2.D7, U1.DS
  N8: Part2.B-, M1.pin_2
  N9: Part2.B+, M1.pin_1
  N10: Part2.A-, M2.pin_2
  N11: Part2.A+, M2.pin_1
  N12: Part2.VMOT, VCC3.+, VCC4.+
  N13: U1.Q1, LED5.A
  N14: U1.Q2, LED4.A
  N15: U1.Q3, LED3.A
  N16: U1.Q4, LED2.A
  N17: U1.Q5, LED1.A
  GND: U1.GND, R2.Pin_1, R3.Pin_1, R4.Pin_1, R5.Pin_1, R6.Pin_1, HC-SR04_Sensor_1.GND, IR_Reflectance_Sensor_Front.E, IR_Reflectance_Sensor_Front.K, IR_Reflectance_Sensor_Left.E, IR_Reflectance_Sensor_Left.K, IR_Reflectance_Right.E, IR_Reflectance_Right.K
  N18: LED1.C, R6.Pin_0
  N19: LED2.C, R5.Pin_0
  N20: LED3.C, R4.Pin_0
  N21: LED4.C, R3.Pin_0
  N22: LED5.C, R2.Pin_0
